# Fritzing sketch Pegaus Wiring Diagram (saved by Fritzing 0.9.9b)
breadboards: 1

parts:
  Part1 = TXB0104 4-channel Bi-Directional Level Shifter
  Part2 = Adafruit HUZZAH32 ESP32 Feather [part_number="Adafruit #3405"]
  Part4 = VERTER 5V USB Buck-Boost
  X1 = USB Connectors [package=usb-a-s-nosilk-female]

nets:
  N1: Part1.HV, Part2.VBUS, Part4.5.0V, X1.VBUS
  GND: Part1.GND, Part2.GND, Part4.GND, X1.GND
  N2: Part1.A2, Part2.IO21
  N3: Part1.A1, Part2.IO17
  N4: Part1.LV, Part2.3.3V

custom parts:
  TXB0104 4-channel Bi-Directional Level Shifter: Because the Arduino (and Basic Stamp) are 5V devices, and most modern sensors, displays, flash cards and modes are 3.3V-only, many makers find that they need to perform level shifting/conversion to protect the 3.3V device from 5V. Although one can use resistors to make a divider, for high speed transfers, the resistors can add a lot of slew and cause havoc that is tough to debug. For that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
  VERTER 5V USB Buck-Boost: VERTER can take battery voltages from 3-12VDC and output a nice 5V DC, which makes it a perfect universal power supply for your portable project! Where Verter really shines is when you have a battery or power range that can fluctuate a lot, or you don't know what you'll end up using.
